# Fritzing sketch Projecto_cilindro (saved by Fritzing 0.9.6b)
breadboards: 1

parts:
  HC-SR04_Sensor_1 = HC-SR04 Ultrasonic Distance Sensor
  Raspberry_Pi1 = Raspberry Pi 2
  R1 = Resistor [tolerance=±5% power=0.25 resistance=220 package=THT]
  J2 = Dagu DGServo 9g header connector (female) [package=THT]

nets:
  VCC: HC-SR04_Sensor_1.VCC, Raspberry_Pi1.5V, J2.Vcc
  N1: HC-SR04_Sensor_1.TRIG, Raspberry_Pi1.GPIO23
  N2: HC-SR04_Sensor_1.ECHO, R1.Pin_1
  GND: HC-SR04_Sensor_1.GND, Raspberry_Pi1.GND
  N3: Raspberry_Pi1.GPIO17, J2.gnd

notes:
  Medição de avanço e recuo de um cilindro
  Tensão de saída para cilindro
  Pinout Raspberry:
  Entrada: GPIO 23 - Trigger
  Entrada: GPIO 24 - Echo
  Saída: GPIO 17 - Saída em PWD (3,3-5Vdc)
